# Fritzing sketch schematics (saved by Fritzing 0.9.3b)

parts:
  Bauteil1 = Arduino Nano (Rev3.0)
  Relay = KY-019 5V Relay Module [package="Breakout board"]
  Pump = DC Motor
  433MHz_TX = FS1000A - 433Mhz RF Transmitter [package=THT]
  +12V = Power Jack [package=power_jack_slot]
  R1 = Resistor [tolerance=±5% resistance=10k package=THT]
  D1 = Rectifier Diode [part_number=1N4001 package="300 mil [THT]"]
  LED1 = LED - 5mm [color="Blue (505nm)" package="5 mm [THT]"]
  C1 = Electrolytic Capacitor [capacitance=47µF voltage=50V package="100 mil [THT, electrolytic]"]
  C2 = Ceramic Capacitor [capacitance=1nF package="100 mil [THT, multilayer]"]
  R2 = Resistor [tolerance=±5% resistance=10 package=THT]
  C3 = Electrolytic Capacitor [capacitance=1µF package="100 mil [THT, electrolytic]"]
  Humidity_Contacts = Screw terminal - 2 pins [package=THT]

nets:
  GND: Bauteil1.GND, Relay.-, Pump.pin_2, 433MHz_TX.GND, +12V.GND, LED1.cathode, C1.-, C2.0
  N1: Bauteil1.D8, 433MHz_TX.DATA
  N2: Bauteil1.D9, 433MHz_TX.VCC
  N3: Bauteil1.D11/MOSI, Humidity_Contacts.pin1
  N4: Bauteil1.D12/MISO, Relay.S
  N5: Bauteil1.VIN, D1.cathode, C1.+
  N6: Bauteil1.5V, Relay.+
  N7: Bauteil1.A0, Humidity_Contacts.pin2
  N8: Bauteil1.D13/SCK, R1.Pin_0
  N9: Relay.Common, +12V.PWR, D1.anode, R2.Pin_0
  N10: Relay.NO, Pump.pin_1, C2.1, C3.-
  N11: R1.Pin_1, LED1.anode
  N12: R2.Pin_1, C3.+

custom parts:
  KY-019 5V Relay Module: KY-019 5V Relay module, used to control AC circuits. (Special thanks to vanepp for fixing the PCB holes and other errors)
  FS1000A - 433Mhz RF Transmitter: This is 433Mhz RF transmitter with receiver kit for Arduino ARM MCU wireless Application environment: Remote control switch, receiver module, motorcycles, automobile anti-theft products, home security products, electric doors, shutter doors, windows, remote control socket, remote control LED, remote audio remote control electric doors, garage door remote control, remote control retractable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
